# Fritzing sketch SnowDay (saved by Fritzing 0.9.2b)
breadboards: 1

parts:
  NeoPixelRing = Neopixel Ring 16
  LDR = Photocell (LDR) [package=THT]
  Spark_Photon = Spark Core (v1.0)
  R3 = Resistor [tolerance=±5% resistance=220 package=THT]

nets:
  GND: NeoPixelRing.GND, Spark_Photon.GND, R3.Pin_0
  VCC: NeoPixelRing.VCC, Spark_Photon.VIN
  N1: NeoPixelRing.IN, Spark_Photon.D2
  N2: LDR.pin_0, Spark_Photon.A5
  N3: LDR.pin_1, Spark_Photon.A0, R3.Pin_1

custom parts:
  Neopixel Ring 16: Neopixel Ring x16
